# Fritzing sketch FIRST2017ScoutingDevice (saved by Fritzing 0.9.3b)
circuit board: 8.46667cm x 5.64444cm
breadboards: 1

parts:
  Part1 = Arduino Uno (Rev3)
  LCD1 = LCD screen
  LED2 = LED - 5mm [color="Red (633nm)" package="5 mm [THT]"]
  R1 = Resistor [tolerance=±5% resistance=220 package=THT]
  R2 = Resistor [tolerance=±5% resistance=220 package=THT]
  LED3 = LED - 5mm [color="Yellow (585nm)" package="5 mm [THT]"]
  LED4 = LED - 5mm [color="Green (570nm)" package="5 mm [THT]"]
  LED5 = LED - 5mm [color="Blue (470nm)" package="5 mm [THT]"]
  R3 = Resistor [tolerance=±5% resistance=220 package=THT]
  R4 = Resistor [tolerance=±5% resistance=220 package=THT]
  R5 = Resistor [tolerance=±5% resistance=220 package=THT]
  S1 = Pushbutton [package="[THT]"]
  S2 = Pushbutton [package="[THT]"]
  S3 = Pushbutton [package="[THT]"]
  S4 = Pushbutton [package="[THT]"]
  S5 = Pushbutton [package="[THT]"]
  LED1 = smd LED [color="White (6500K)" package="1206 [SMD]"]
  S7 = Pushbutton [package="[THT]"]
  R7 = Trimmer Potentiometer [maximum_resistance=10kΩ package=THT]
  R6 = Trimmer Potentiometer [maximum_resistance=10kΩ package=THT]

nets:
  N1: Part1.A0, LED1.cathode
  N2: Part1.A1, LED2.cathode
  N3: Part1.A2, LED3.cathode
  N4: Part1.A3, LED4.cathode
  N5: Part1.A4/SDA, LED5.cathode
  N6: Part1.D8, LCD1.E
  N7: Part1.D9_PWM, LCD1.DB4
  N8: Part1.D10_PWM/SS, LCD1.DB5
  N9: Part1.D11_PWM/MOSI, LCD1.DB6
  N10: Part1.D12/MISO, LCD1.DB7
  N11: Part1.D0/RX, S7.Pin_3, S7.Pin_4
  N12: Part1.D2, S1.Pin_3, S1.Pin_4
  N13: Part1.D3_PWM, S2.Pin_3, S2.Pin_4
  N14: Part1.D4, S3.Pin_3, S3.Pin_4
  N15: Part1.D5_PWM, S4.Pin_3, S4.Pin_4
  N16: Part1.D6_PWM, S5.Pin_3, S5.Pin_4
  N17: Part1.D7, LCD1.RS
  5V: Part1.5V, LCD1.VDD, R7.leg1, R6.leg1
  GND: Part1.GND, LCD1.VSS, LCD1.R/W, LCD1.LED-, R1.Pin_1, R2.Pin_1, R3.Pin_1, R4.Pin_1, R5.Pin_1, S1.Pin_1, S1.Pin_2, S2.Pin_1, S2.Pin_2, S3.Pin_1, S3.Pin_2, S4.Pin_1, S4.Pin_2, S5.Pin_1, S5.Pin_2, S7.Pin_1, S7.Pin_2, R7.leg2, R6.leg2
  N18: LCD1.V0, R7.wiper
  N19: LCD1.LED+, R6.wiper
  N20: LED2.anode, R2.Pin_0
  N21: R1.Pin_0, LED1.anode
  N22: LED3.anode, R3.Pin_0
  N23: LED4.anode, R4.Pin_0
  N24: LED5.anode, R5.Pin_0
